# Fritzing sketch IronMansChestLight (saved by Fritzing 0.9.2b)
circuit board: 8.46667cm x 5.64444cm
breadboards: 1

parts:
  Bauteil1 = Arduino Nano (Rev3.0)
  Bauteil2 = 12 NeoPixel Ring [part_number=1643]

nets:
  GND: Bauteil1.GND, Bauteil2.GND
  N1: Bauteil1.D9, Bauteil2.IN
  5V: Bauteil1.5V, Bauteil2.VDD

custom parts:
  12 NeoPixel Ring: 12 ultra bright smart LED NeoPixels are arranged in a circle with 1.5" (37mm) outer diameter. The rings are 'chainable' - connect the output pin of one to the input pin of another. Use only one microcontroller pin to control as many as you can chain together! Each LED is addressable as the driver chip is inside the LED. Each one has ~18mA constant current drive so the color will be very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
